// Logisim project 1-b-ALU.circ as structural Verilog: 1 circuit, main circuit main
module main (
  input  cin,
  input  [1:0] operation,
  input  Binvert,
  input  a,
  input  b,
  output result,
  output cout
);

  wire _1_b_adder_carryout, and_1_out, multiplexer_1_out, not_1_out, or_1_out;

  not not_1 (not_1_out, b);
  Multiplexer #(.enable("false")) multiplexer_1 (.in0(b), .in1(not_1_out), .out(multiplexer_1_out), .sel(Binvert));
  and and_1 (and_1_out, a, multiplexer_1_out);
  or or_1 (or_1_out, a, multiplexer_1_out);
  _1_bit_adder_main _1_b_adder (
    .CarryIn(cin), .a(a), .b(multiplexer_1_out), .CarryOut(_1_b_adder_carryout), .SumOut(cout));
  _3_to_1_multiplexor_main _3_1_mux (
    .in_2(and_1_out), .in_3(or_1_out), .in_4(_1_b_adder_carryout), .in_1(operation), .out_5(result));
endmodule
