// Logisim project 1-bit-adder.circ as structural Verilog: 1 circuit, main circuit main
module main (
  input  CarryIn,
  input  a,
  input  b,
  output CarryOut,
  output SumOut
);

  wire and_1_out, and_2_out, and_3_out, and_4_out, and_5_out, and_6_out, and_7_out, and_8_out, not_1_out,
       not_2_out, not_3_out, not_4_out, not_5_out, not_6_out, not_7_out, not_8_out, not_9_out;

  not not_1 (not_1_out, CarryIn);
  not not_2 (not_2_out, a);
  not not_3 (not_3_out, b);
  not not_4 (not_4_out, CarryIn);
  not not_5 (not_5_out, a);
  not not_6 (not_6_out, CarryIn);
  not not_7 (not_7_out, b);
  not not_8 (not_8_out, a);
  not not_9 (not_9_out, b);
  and and_1 (and_1_out, not_1_out, a, b);
  and and_2 (and_2_out, CarryIn, not_2_out, b);
  and and_3 (and_3_out, CarryIn, a, not_3_out);
  and and_4 (and_4_out, CarryIn, a, b);
  and and_5 (and_5_out, not_4_out, not_5_out, b);
  and and_6 (and_6_out, not_6_out, a, not_7_out);
  and and_7 (and_7_out, CarryIn, not_8_out, not_9_out);
  and and_8 (and_8_out, CarryIn, a, b);
  or or_1 (CarryOut, and_1_out, and_2_out, and_3_out, and_4_out);
  or or_2 (SumOut, and_5_out, and_6_out, and_7_out, and_8_out);
endmodule
