// Logisim project 1-bit-alu.circ as structural Verilog: 1 circuit, main circuit main
module main (
  input  Binvert,
  input  CarryIn,
  input  [1:0] Operation,
  input  a,
  input  b,
  output Result,
  output CarryOut
);

  wire and_1_out, main_1_sumout, multiplexer_1_out, not_1_out, or_1_out;

  Multiplexer multiplexer_1 (.in0(b), .in1(not_1_out), .out(multiplexer_1_out), .sel(Binvert));  // open: en
  not not_1 (not_1_out, b);
  and and_1 (and_1_out, a, multiplexer_1_out);
  or or_1 (or_1_out, a, multiplexer_1_out);
  _1_bit_adder_main main_1 (
    .CarryIn(CarryIn), .a(a), .b(multiplexer_1_out), .CarryOut(CarryOut), .SumOut(main_1_sumout));
  _3_input_multiplexor_main main_2 (
    .AND(and_1_out), .OR(or_1_out), .Result_Adder(main_1_sumout), .Operation(Operation), .Result(Result));
endmodule
