// Logisim project 2by2reg.circ as structural Verilog: 1 circuit, main circuit main
module main (
  input  in_1,
  input  [1:0] in_2,
  output [1:0] out_3,
  output [1:0] out_4,
  output [1:0] out_5
);

  wire clock_1_out, decoder_1_out0, decoder_1_out1;

  Clock clock_1 (.out(clock_1_out));
  Decoder #(.enable("false")) decoder_1 (.out0(decoder_1_out0), .out1(decoder_1_out1), .sel(in_1));
  Multiplexer #(.width(2)) multiplexer_1 (.in0(out_4), .in1(out_5), .out(out_3), .sel(in_1));  // open: en
  register_WE_main main_1 (.in_2(in_2), .in_3(clock_1_out), .out_4(out_4), .in_1(decoder_1_out0));
  register_WE_main main_2 (.in_2(in_2), .in_3(clock_1_out), .out_4(out_5), .in_1(decoder_1_out1));
endmodule
