// Logisim project 3-input-multiplexor.circ as structural Verilog: 1 circuit, main circuit main
module main (
  input  [1:0] Operation,
  input  AND,
  input  OR,
  input  Result_Adder,
  output Result
);

  wire and_1_out, and_2_out, and_3_out, not_1_out, not_2_out, not_3_out, not_4_out;

  not not_1 (not_1_out, Operation[0]);
  not not_2 (not_2_out, Operation[1]);
  not not_3 (not_3_out, Operation[1]);
  not not_4 (not_4_out, Operation[0]);
  and and_1 (and_1_out, AND, not_1_out, not_2_out);
  and and_2 (and_2_out, OR, Operation[0], not_3_out);
  and and_3 (and_3_out, Result_Adder, not_4_out, Operation[1]);
  or or_1 (Result, and_1_out, and_2_out, and_3_out);
endmodule
