// Logisim project 3-to-1-multiplexor.circ as structural Verilog: 1 circuit, main circuit main
module main (
  input  [1:0] in_1,
  input  in_2,
  input  in_3,
  input  in_4,
  output out_5
);

  wire and_1_out, and_2_out, and_3_out, not_1_out, not_2_out, not_3_out, not_4_out;

  not not_1 (not_1_out, in_1[0]);
  not not_2 (not_2_out, in_1[1]);
  not not_3 (not_3_out, in_1[1]);
  not not_4 (not_4_out, in_1[0]);
  and and_1 (and_1_out, in_2, not_1_out, not_2_out);
  and and_2 (and_2_out, in_3, in_1[0], not_3_out);
  and and_3 (and_3_out, in_4, not_4_out, in_1[1]);
  or or_1 (out_5, and_1_out, and_2_out, and_3_out);
endmodule
