// Logisim project 4_bit_ALU.circ as structural Verilog: 1 circuit, main circuit main
module main (
  input  in_1,
  input  [1:0] in_2,
  input  [3:0] in_3,
  input  [3:0] in_4,
  output [3:0] out_5,
  output out_6
);

  wire main_1_cout, main_2_cout, main_3_cout;

  _1_b_ALU_main main_1 (
    .a(in_3[0]), .b(in_4[0]), .Binvert(in_1), .cin(in_1), .operation(in_2), .cout(main_1_cout),
    .result(out_5[0]));
  _1_b_ALU_main main_2 (
    .a(in_3[1]), .b(in_4[1]), .Binvert(in_1), .cin(main_1_cout), .operation(in_2), .cout(main_2_cout),
    .result(out_5[1]));
  _1_b_ALU_main main_3 (
    .a(in_3[2]), .b(in_4[2]), .Binvert(in_1), .cin(main_2_cout), .operation(in_2), .cout(main_3_cout),
    .result(out_5[2]));
  _1_b_ALU_main main_4 (
    .a(in_3[3]), .b(in_4[3]), .Binvert(in_1), .cin(main_3_cout), .operation(in_2), .cout(out_6),
    .result(out_5[3]));
endmodule
