// Logisim project 4a.circ as structural Verilog: 1 circuit, main circuit main
module main (
  input  R,
  input  WE,
  input  S,
  output Q,
  output NotQ
);

  wire and_1_out, and_2_out, and_3_out, and_4_out;

  and and_1 (and_1_out, R, WE);
  buf and_2 (and_2_out, NotQ);  // AND_Gate
  buf and_3 (and_3_out, Q);  // AND_Gate
  and and_4 (and_4_out, WE, S, S);
  nor nor_1 (Q, and_1_out, and_2_out);
  nor nor_2 (NotQ, and_3_out, and_4_out);
endmodule
