// Logisim project 4b.circ as structural Verilog: 1 circuit, main circuit main
module main (
  input  in_1
);

  wire main_1_out_3, main_2_out_3, not_1_out, not_2_out, or_1_out;

  not not_1 (not_1_out, in_1);
  d_flip_flop_main main_1 (.in_1(not_1_out), .in_2(not_2_out), .out_3(main_1_out_3));  // open: out_4
  d_flip_flop_main main_2 (.in_1(in_1), .in_2(not_2_out), .out_3(main_2_out_3));  // open: out_4
  or or_1 (or_1_out, main_1_out_3, main_2_out_3);
  not not_2 (not_2_out, or_1_out);
endmodule
