// Logisim project cpu32.circ as structural Verilog: 7 circuits, main circuit ALU
module InstructionDecode (
  input  [31:0] Instruction,
  output [5:0] op,
  output [4:0] rs,
  output [4:0] rt,
  output [4:0] rd,
  output [4:0] shamt,
  output [5:0] funct,
  output [15:0] immediate,
  output [25:0] address
);


  assign address = Instruction[25:0];
  assign funct = Instruction[5:0];
  assign immediate = Instruction[15:0];
  assign op = Instruction[31:26];
  assign rd = Instruction[15:11];
  assign rs = Instruction[25:21];
  assign rt = Instruction[20:16];
  assign shamt = Instruction[10:6];

  // Notes on the sheet:
  //   I-type
  //   J-type
  //   R-type
endmodule

module Registers (
  input  [4:0] ReadRegister1,
  input  [4:0] ReadRegister2,
  input  [4:0] WriteRegister,
  input  [31:0] WriteData,
  input  Clock,
  input  RegWrite,
  input  Clear,
  output [31:0] ReadData1,
  output [31:0] ReadData2
);

  wire decoder_1_out0, decoder_1_out1, decoder_1_out2, decoder_1_out3, decoder_1_out4, decoder_1_out5,
       decoder_1_out6, decoder_1_out7;
  wire [31:0] registers4_1_readdata1, registers4_1_readdata2, registers4_2_readdata1, registers4_2_readdata2,
       registers4_3_readdata1, registers4_3_readdata2, registers4_4_readdata1, registers4_4_readdata2,
       registers4_5_readdata1, registers4_5_readdata2, registers4_6_readdata1, registers4_6_readdata2,
       registers4_7_readdata1, registers4_7_readdata2, registers4z_1_readdata1, registers4z_1_readdata2;

  Decoder #(.select(3), .disabled(0)) decoder_1 (
    .out0(decoder_1_out0), .out1(decoder_1_out1), .out2(decoder_1_out2), .out3(decoder_1_out3),
    .out4(decoder_1_out4), .out5(decoder_1_out5), .out6(decoder_1_out6), .out7(decoder_1_out7),
    .sel(WriteRegister[4:2]), .en(RegWrite));
  Registers4Z registers4z_1 (
    .ReadRegister1(ReadRegister1[1:0]), .ReadRegister2(ReadRegister2[1:0]),
    .WriteRegister(WriteRegister[1:0]), .WriteData(WriteData), .RegWrite(decoder_1_out0), .Clear(Clear),
    .Clock(Clock), .ReadData1(registers4z_1_readdata1), .ReadData2(registers4z_1_readdata2));
  Registers4 registers4_1 (
    .ReadRegister1(ReadRegister1[1:0]), .ReadRegister2(ReadRegister2[1:0]),
    .WriteRegister(WriteRegister[1:0]), .WriteData(WriteData), .RegWrite(decoder_1_out1), .Clear(Clear),
    .Clock(Clock), .ReadData1(registers4_1_readdata1), .ReadData2(registers4_1_readdata2));
  Registers4 registers4_2 (
    .ReadRegister1(ReadRegister1[1:0]), .ReadRegister2(ReadRegister2[1:0]),
    .WriteRegister(WriteRegister[1:0]), .WriteData(WriteData), .RegWrite(decoder_1_out2), .Clear(Clear),
    .Clock(Clock), .ReadData1(registers4_2_readdata1), .ReadData2(registers4_2_readdata2));
  Registers4 registers4_3 (
    .ReadRegister1(ReadRegister1[1:0]), .ReadRegister2(ReadRegister2[1:0]),
    .WriteRegister(WriteRegister[1:0]), .WriteData(WriteData), .RegWrite(decoder_1_out3), .Clear(Clear),
    .Clock(Clock), .ReadData1(registers4_3_readdata1), .ReadData2(registers4_3_readdata2));
  Registers4 registers4_4 (
    .ReadRegister1(ReadRegister1[1:0]), .ReadRegister2(ReadRegister2[1:0]),
    .WriteRegister(WriteRegister[1:0]), .WriteData(WriteData), .RegWrite(decoder_1_out4), .Clear(Clear),
    .Clock(Clock), .ReadData1(registers4_4_readdata1), .ReadData2(registers4_4_readdata2));
  Registers4 registers4_5 (
    .ReadRegister1(ReadRegister1[1:0]), .ReadRegister2(ReadRegister2[1:0]),
    .WriteRegister(WriteRegister[1:0]), .WriteData(WriteData), .RegWrite(decoder_1_out5), .Clear(Clear),
    .Clock(Clock), .ReadData1(registers4_5_readdata1), .ReadData2(registers4_5_readdata2));
  Registers4 registers4_6 (
    .ReadRegister1(ReadRegister1[1:0]), .ReadRegister2(ReadRegister2[1:0]),
    .WriteRegister(WriteRegister[1:0]), .WriteData(WriteData), .RegWrite(decoder_1_out6), .Clear(Clear),
    .Clock(Clock), .ReadData1(registers4_6_readdata1), .ReadData2(registers4_6_readdata2));
  Registers4 registers4_7 (
    .ReadRegister1(ReadRegister1[1:0]), .ReadRegister2(ReadRegister2[1:0]),
    .WriteRegister(WriteRegister[1:0]), .WriteData(WriteData), .RegWrite(decoder_1_out7), .Clear(Clear),
    .Clock(Clock), .ReadData1(registers4_7_readdata1), .ReadData2(registers4_7_readdata2));
  Multiplexer #(.select(3), .width(32), .enable("false")) multiplexer_1 (
    .in0(registers4z_1_readdata1), .in1(registers4_1_readdata1), .in2(registers4_2_readdata1),
    .in3(registers4_3_readdata1), .in4(registers4_4_readdata1), .in5(registers4_5_readdata1),
    .in6(registers4_6_readdata1), .in7(registers4_7_readdata1), .out(ReadData1), .sel(ReadRegister1[4:2]));
  Multiplexer #(.select(3), .width(32), .enable("false")) multiplexer_2 (
    .in0(registers4z_1_readdata2), .in1(registers4_1_readdata2), .in2(registers4_2_readdata2),
    .in3(registers4_3_readdata2), .in4(registers4_4_readdata2), .in5(registers4_5_readdata2),
    .in6(registers4_6_readdata2), .in7(registers4_7_readdata2), .out(ReadData2), .sel(ReadRegister2[4:2]));
endmodule

module SignExtend (
  input  [15:0] in_1,
  output [31:0] out_2
);


  assign out_2 = {{17{in_1[15]}}, in_1[14:0]};
endmodule

module ALU (
  input  [31:0] A,
  input  [31:0] B,
  input  [3:0] Operation,
  output Zero,
  output [31:0] Result,
  output Overflow
);

  wire getsign_1_sign, getsign_2_sign, getsign_3_sign;
  wire [31:0] adder_1_out, and_1_out, getsign_1_out_2, getsign_2_out_2, getsign_3_out_2, multiplexer_1_out,
       multiplexer_2_out, not_1_out, not_2_out, or_1_out, setlsb_1_out_3;

  assign not_1_out = ~A;  // NOT_Gate not_1, 32 bits wide
  assign not_2_out = ~B;  // NOT_Gate not_2, 32 bits wide
  Multiplexer #(.width(32), .enable("false")) multiplexer_1 (
    .in0(A), .in1(not_1_out), .out(multiplexer_1_out), .sel(Operation[3]));
  Multiplexer #(.width(32), .enable("false")) multiplexer_2 (
    .in0(B), .in1(not_2_out), .out(multiplexer_2_out), .sel(Operation[2]));
  GetSign getsign_1 (.in_1(multiplexer_1_out), .Sign(getsign_1_sign), .out_2(getsign_1_out_2));
  GetSign getsign_2 (.in_1(multiplexer_2_out), .Sign(getsign_2_sign), .out_2(getsign_2_out_2));
  Overflow overflow_1 (
    .A(getsign_1_sign), .B(getsign_2_sign), .Result(getsign_3_sign), .Operation(Operation[1:0]),
    .Overflow(Overflow));
  assign and_1_out = getsign_1_out_2 & getsign_2_out_2;  // AND_Gate and_1, 32 bits wide
  assign or_1_out = getsign_1_out_2 | getsign_2_out_2;  // OR_Gate or_1, 32 bits wide
  Adder #(.width(32)) adder_1 (
    .a(getsign_1_out_2), .b(getsign_2_out_2), .out(adder_1_out), .cin(Operation[2]));  // open: cout
  GetSign getsign_3 (.in_1(adder_1_out), .Sign(getsign_3_sign), .out_2(getsign_3_out_2));
  SetLSB setlsb_1 (.in_2({32{1'b0}}), .LSB(getsign_3_sign), .out_3(setlsb_1_out_3));
  Multiplexer #(.select(2), .width(32), .enable("false")) multiplexer_3 (
    .in0(and_1_out), .in1(or_1_out), .in2(getsign_3_out_2), .in3(setlsb_1_out_3), .out(Result),
    .sel(Operation[1:0]));
  Zero zero_1 (.in_1(Result), .out_2(Zero));

  // Notes on the sheet:
  //   +/-
  //   +/-
  //   +/-
  //   LSB
  //   0?
endmodule

module ShiftLeft2 (
  input  [31:0] Input,
  output [31:0] Result
);


  assign Result = {Input[29:0], 2'b00};
endmodule

module JumpAddress (
  input  [25:0] Address,
  input  [31:0] PC_4,
  output [31:0] JumpAddress
);


  assign JumpAddress = {PC_4[31:28], Address, 2'b00};
endmodule

module ALUadd (
  input  [31:0] A,
  input  [31:0] B,
  output [31:0] Result,
  output Overflow
);

  ALU alu_1 (.A(A), .B(B), .Operation(4'b0010), .Result(Result), .Overflow(Overflow));  // open: Zero
endmodule
