// Logisim project d_flip_flop.circ as structural Verilog: 1 circuit, main circuit main
module main (
  input  in_1,
  input  in_2,
  output out_3,
  output out_4
);

  wire main_1_out_3, not_1_out;

  not not_1 (not_1_out, in_1);
  d_latch_main main_1 (.C(in_1), .D(in_2), .out_3(main_1_out_3));  // open: out_4
  d_latch_main main_2 (.C(not_1_out), .D(main_1_out_3), .out_3(out_3), .out_4(out_4));
endmodule
