// Logisim project d_latch.circ as structural Verilog: 1 circuit, main circuit main
module main (
  input  C,
  input  D,
  output out_3,
  output out_4
);

  wire and_1_out, and_2_out, not_1_out, or_1_out, or_2_out;

  and and_1 (and_1_out, C, not_1_out);
  not not_1 (not_1_out, D);
  and and_2 (and_2_out, C, D);
  not not_2 (out_3, or_1_out);
  or or_1 (or_1_out, and_1_out, out_4);
  or or_2 (or_2_out, and_2_out, out_3);
  not not_3 (out_4, or_2_out);
endmodule
