// Logisim project misc32.circ as structural Verilog: 8 circuits, main circuit GetSign
module GetSign (
  input  [31:0] in_1,
  output [31:0] out_2,
  output Sign
);


  assign out_2 = in_1;
  assign Sign = in_1[31];
endmodule

module SetLSB (
  input  LSB,
  input  [31:0] in_2,
  output [31:0] out_3
);


  assign out_3 = {in_2[31:1], LSB};
endmodule

module Zero (
  input  [31:0] in_1,
  output out_2
);

  wire or_1_out, or_2_out, or_3_out, or_4_out;

  or or_1 (or_1_out, in_1[0], in_1[1], in_1[2], in_1[3], in_1[4], in_1[5], in_1[6]);
  or or_2 (or_2_out, in_1[7], in_1[8], in_1[9], in_1[10], in_1[11], in_1[12], in_1[13], in_1[14], in_1[15]);
  or or_3 (or_3_out, in_1[16], in_1[17], in_1[18], in_1[19], in_1[20], in_1[21], in_1[22], in_1[23], in_1[24]);
  or or_4 (or_4_out, in_1[25], in_1[26], in_1[27], in_1[28], in_1[29], in_1[30], in_1[31]);
  nor nor_1 (out_2, or_1_out, or_2_out, or_3_out, or_4_out);
endmodule

module Overflow (
  input  Result,
  input  A,
  input  B,
  input  [1:0] Operation,
  output Overflow
);

  wire and_1_out, and_2_out, not_1_out, not_2_out, not_3_out, or_1_out;

  not not_1 (not_1_out, Result);
  not not_2 (not_2_out, A);
  not not_3 (not_3_out, B);
  and and_1 (and_1_out, not_1_out, A, B);
  and and_2 (and_2_out, Result, not_2_out, not_3_out);
  or or_1 (or_1_out, and_1_out, and_2_out);
  and and_3 (Overflow, or_1_out, Operation[1]);
endmodule

module Registers4 (
  input  Clock,
  input  [1:0] ReadRegister1,
  input  [1:0] ReadRegister2,
  input  [1:0] WriteRegister,
  input  [31:0] WriteData,
  input  RegWrite,
  input  Clear,
  output [31:0] ReadData1,
  output [31:0] ReadData2
);

  wire decoder_1_out0, decoder_1_out1, decoder_1_out2, decoder_1_out3;
  wire [31:0] register_1_q, register_2_q, register_3_q, register_4_q;

  Decoder #(.select(2), .disabled(0)) decoder_1 (
    .out0(decoder_1_out0), .out1(decoder_1_out1), .out2(decoder_1_out2), .out3(decoder_1_out3),
    .sel(WriteRegister), .en(RegWrite));
  Register #(.width(32)) register_1 (.D(WriteData), .en(decoder_1_out0), .Q(register_1_q), .clk(Clock), .clr(Clear));
  Register #(.width(32)) register_2 (.D(WriteData), .en(decoder_1_out1), .Q(register_2_q), .clk(Clock), .clr(Clear));
  Register #(.width(32)) register_3 (.D(WriteData), .en(decoder_1_out2), .Q(register_3_q), .clk(Clock), .clr(Clear));
  Register #(.width(32)) register_4 (.D(WriteData), .en(decoder_1_out3), .Q(register_4_q), .clk(Clock), .clr(Clear));
  Multiplexer #(.select(2), .width(32), .enable("false")) multiplexer_1 (
    .in0(register_1_q), .in1(register_2_q), .in2(register_3_q), .in3(register_4_q), .out(ReadData1),
    .sel(ReadRegister1));
  Multiplexer #(.select(2), .width(32), .enable("false")) multiplexer_2 (
    .in0(register_1_q), .in1(register_2_q), .in2(register_3_q), .in3(register_4_q), .out(ReadData2),
    .sel(ReadRegister2));
endmodule

module Registers4Z (
  input  Clock,
  input  [1:0] ReadRegister1,
  input  [1:0] ReadRegister2,
  input  [1:0] WriteRegister,
  input  [31:0] WriteData,
  input  RegWrite,
  input  Clear,
  output [31:0] ReadData1,
  output [31:0] ReadData2
);

  wire decoder_1_out1, decoder_1_out2, decoder_1_out3;
  wire [31:0] register_1_q, register_2_q, register_3_q;

  Decoder #(.select(2), .disabled(0)) decoder_1 (
    .out1(decoder_1_out1), .out2(decoder_1_out2), .out3(decoder_1_out3), .sel(WriteRegister), .en(RegWrite));  // open: out0
  Register #(.width(32)) register_1 (.D(WriteData), .en(decoder_1_out1), .Q(register_1_q), .clk(Clock), .clr(Clear));
  Register #(.width(32)) register_2 (.D(WriteData), .en(decoder_1_out2), .Q(register_2_q), .clk(Clock), .clr(Clear));
  Register #(.width(32)) register_3 (.D(WriteData), .en(decoder_1_out3), .Q(register_3_q), .clk(Clock), .clr(Clear));
  Multiplexer #(.select(2), .width(32), .enable("false")) multiplexer_1 (
    .in0({32{1'b0}}), .in1(register_1_q), .in2(register_2_q), .in3(register_3_q), .out(ReadData1),
    .sel(ReadRegister1));
  Multiplexer #(.select(2), .width(32), .enable("false")) multiplexer_2 (
    .in0({32{1'b0}}), .in1(register_1_q), .in2(register_2_q), .in3(register_3_q), .out(ReadData2),
    .sel(ReadRegister2));
endmodule

module WordAddress (
  input  [31:0] ByteAddress,
  output WordAligned,
  output [7:0] WordAddress
);

  nor nor_1 (WordAligned, ByteAddress[0], ByteAddress[1]);

  assign WordAddress = ByteAddress[9:2];
endmodule

module MemoryData (
  input  [31:0] WriteData,
  input  [31:0] FromMemory,
  input  Write,
  input  Read,
  output [31:0] ReadData,
  output [31:0] ToMemory
);

  wire not_1_out, not_2_out;

  not not_1 (not_1_out, Write);
  not not_2 (not_2_out, Read);
  assign ReadData = not_1_out ? FromMemory : 32'bz;  // Controlled_Buffer controlled_buffer_1
  assign ToMemory = not_2_out ? WriteData : 32'bz;  // Controlled_Buffer controlled_buffer_2
endmodule
