// Logisim project processor.circ as structural Verilog: 3 circuits, main circuit Datapath
module Datapath (
  input  Clock,
  input  Reset
);

  wire ALU_zero, and_1_out, Control_alusrc, Control_branch, Control_memread, Control_memtoreg,
       Control_memwrite, Control_regdst, Control_regwrite;
  wire [1:0] Control_aluop;
  wire [3:0] ALU_control_operation;
  wire [4:0] Instruction_decode_rd, Instruction_decode_rs, Instruction_decode_rt, multiplexer_1_out;
  wire [5:0] Instruction_decode_funct, Instruction_decode_op;
  wire [7:0] wordaddress_1_wordaddress, wordaddress_2_wordaddress;
  wire [15:0] Instruction_decode_immediate;
  wire [31:0] adder_1_out, ALU_add_result, ALU_result, multiplexer_2_out, multiplexer_3_out,
       multiplexer_4_out, PC_q, ram_1_data, ram_2_data, Registers_readdata1, Registers_readdata2,
       shifter_1_out, Sign_extend_out_2;

  Register #(.width(32)) PC (.D(multiplexer_3_out), .Q(PC_q), .clk(Clock), .clr(Reset));  // open: en
  WordAddress wordaddress_1 (.ByteAddress(PC_q), .WordAddress(wordaddress_1_wordaddress));  // open: WordAligned
  InstructionDecode Instruction_decode (
    .Instruction(ram_1_data), .op(Instruction_decode_op), .rs(Instruction_decode_rs),
    .rt(Instruction_decode_rt), .rd(Instruction_decode_rd), .funct(Instruction_decode_funct),
    .immediate(Instruction_decode_immediate));  // open: shamt, address
  Adder #(.width(32)) adder_1 (.a(PC_q), .b(32'h4), .out(adder_1_out));  // open: cin, cout
  RAM #(.dataWidth(32)) ram_1 (
    .addr(wordaddress_1_wordaddress), .data(ram_1_data), .sel(1'b1), .clk(1'b0), .ld(1'b1));  // open: clr
  Control Control (
    .op(Instruction_decode_op), .RegDst(Control_regdst), .Branch(Control_branch), .MemRead(Control_memread),
    .MemToReg(Control_memtoreg), .ALUOp(Control_aluop), .MemWrite(Control_memwrite), .ALUSrc(Control_alusrc),
    .RegWrite(Control_regwrite));
  Multiplexer #(.width(5), .enable("false")) multiplexer_1 (
    .in0(Instruction_decode_rt), .in1(Instruction_decode_rd), .out(multiplexer_1_out), .sel(Control_regdst));
  SignExtend Sign_extend (.in_1(Instruction_decode_immediate), .out_2(Sign_extend_out_2));
  Registers Registers (
    .ReadRegister1(Instruction_decode_rs), .ReadRegister2(Instruction_decode_rt),
    .WriteRegister(multiplexer_1_out), .WriteData(multiplexer_4_out), .Clock(Clock),
    .RegWrite(Control_regwrite), .Clear(Reset), .ReadData1(Registers_readdata1),
    .ReadData2(Registers_readdata2));
  Shifter #(.width(32)) shifter_1 (.in(Sign_extend_out_2), .\dist (5'b00010), .out(shifter_1_out));
  ALUadd ALU_add (.A(adder_1_out), .B(shifter_1_out), .Result(ALU_add_result));  // open: Overflow
  Multiplexer #(.width(32), .enable("false")) multiplexer_2 (
    .in0(Registers_readdata2), .in1(Sign_extend_out_2), .out(multiplexer_2_out), .sel(Control_alusrc));
  ALUcontrol ALU_control (.funct(Instruction_decode_funct), .Operation(ALU_control_operation), .ALUop(Control_aluop));
  WordAddress wordaddress_2 (.ByteAddress(ALU_result), .WordAddress(wordaddress_2_wordaddress));  // open: WordAligned
  and and_1 (and_1_out, Control_branch, ALU_zero);
  ALU ALU (
    .A(Registers_readdata1), .B(multiplexer_2_out), .Operation(ALU_control_operation), .Zero(ALU_zero),
    .Result(ALU_result));  // open: Overflow
  Multiplexer #(.width(32), .enable("false")) multiplexer_3 (
    .in0(adder_1_out), .in1(ALU_add_result), .out(multiplexer_3_out), .sel(and_1_out));
  Multiplexer #(.width(32), .enable("false")) multiplexer_4 (
    .in0(ALU_result), .in1(ram_2_data), .out(multiplexer_4_out), .sel(Control_memtoreg));
  RAM #(.dataWidth(32), .bus("separate")) ram_2 (
    .addr(wordaddress_2_wordaddress), .din(Registers_readdata2), .data(ram_2_data), .str(Control_memwrite),
    .sel(1'b1), .clk(Clock), .ld(Control_memread));  // open: clr

  // Notes on the sheet:
  //   Instruction Memory
  //   Data Memory
endmodule

module Control (
  input  [5:0] op,
  output RegDst,
  output Branch,
  output MemRead,
  output MemToReg,
  output [1:0] ALUOp,
  output MemWrite,
  output ALUSrc,
  output RegWrite
);

  wire addi_out, not_1_out, not_2_out, not_3_out, not_4_out, not_5_out, not_6_out, not_7_out, not_8_out,
       not_9_out, not_10_out, not_11_out, not_12_out, not_13_out, not_14_out, not_15_out, not_16_out,
       not_17_out, not_18_out, not_19_out, not_20_out, not_21_out;

  not not_1 (not_1_out, op[5]);
  not not_2 (not_2_out, op[4]);
  not not_3 (not_3_out, op[0]);
  not not_4 (not_4_out, op[3]);
  not not_5 (not_5_out, op[1]);
  not not_6 (not_6_out, op[2]);
  and R_fmt (ALUOp[1], not_1_out, not_2_out, not_4_out, not_6_out, not_5_out, not_3_out);
  not not_7 (not_7_out, op[4]);
  not not_8 (not_8_out, op[2]);
  not not_9 (not_9_out, op[3]);
  and lw (MemRead, op[5], not_7_out, not_9_out, not_8_out, op[1], op[0]);
  not not_10 (not_10_out, op[4]);
  not not_11 (not_11_out, op[2]);
  and sw (MemWrite, op[5], not_10_out, op[3], not_11_out, op[1], op[0]);
  not not_12 (not_12_out, op[3]);
  not not_13 (not_13_out, op[4]);
  not not_14 (not_14_out, op[5]);
  not not_15 (not_15_out, op[0]);
  not not_16 (not_16_out, op[1]);
  not not_17 (not_17_out, op[5]);
  and beq (ALUOp[0], not_14_out, not_13_out, not_12_out, op[2], not_16_out, not_15_out);
  not not_18 (not_18_out, op[4]);
  not not_19 (not_19_out, op[1]);
  not not_20 (not_20_out, op[0]);
  not not_21 (not_21_out, op[2]);
  and addi (addi_out, not_17_out, not_18_out, op[3], not_21_out, not_19_out, not_20_out);
  or or_1 (ALUSrc, MemRead, addi_out, MemWrite);
  or or_2 (RegWrite, ALUOp[1], addi_out, MemRead);

  assign Branch = ALUOp[0];
  assign MemToReg = MemRead;
  assign RegDst = ALUOp[1];
endmodule

module ALUcontrol (
  input  [1:0] ALUop,
  input  [5:0] funct,
  output [3:0] Operation
);

  wire and_1_out, not_1_out, not_2_out, not_3_out, or_1_out;

  or or_1 (or_1_out, funct[3], funct[0]);
  not not_1 (not_1_out, ALUop[0]);
  and and_1 (and_1_out, ALUop[1], funct[1]);
  not not_2 (not_2_out, ALUop[1]);
  not not_3 (not_3_out, funct[2]);
  and and_2 (Operation[0], ALUop[1], or_1_out);
  and and_3 (Operation[3], ALUop[0], not_1_out);
  or or_2 (Operation[2], ALUop[0], and_1_out);
  or or_3 (Operation[1], not_2_out, not_3_out);
endmodule
