// Logisim project register_WE.circ as structural Verilog: 1 circuit, main circuit main
module main (
  input  in_1,
  input  [1:0] in_2,
  input  in_3,
  output [1:0] out_4
);

  wire [1:0] multiplexer_1_out;

  Multiplexer #(.width(2)) multiplexer_1 (.in0(out_4), .in1(in_2), .out(multiplexer_1_out), .sel(in_1));  // open: en
  d_flip_flop_main main_1 (.in_1(in_3), .in_2(multiplexer_1_out[1]), .out_3(out_4[1]));  // open: out_4
  d_flip_flop_main main_2 (.in_1(in_3), .in_2(multiplexer_1_out[0]), .out_3(out_4[0]));  // open: out_4
endmodule
