// Logisim project two_bit_reg.circ as structural Verilog: 1 circuit, main circuit main
module main (
  input  [1:0] in_1,
  output [1:0] out_2
);

  wire clock_1_out;

  Clock clock_1 (.out(clock_1_out));
  d_flip_flop_main main_1 (.in_1(clock_1_out), .in_2(in_1[1]), .out_3(out_2[1]));  // open: out_4
  d_flip_flop_main main_2 (.in_1(clock_1_out), .in_2(in_1[0]), .out_3(out_2[0]));  // open: out_4
endmodule
